// Logisim project wk6ex3.circ as structural Verilog: 8 circuits, main circuit MyXOR
module MyXOR (
  input  x,
  input  y,
  output o
);

  wire And1_out, And2_out, not_1_out, not_2_out;

  not not_1 (not_1_out, y);
  not not_2 (not_2_out, x);
  and And1 (And1_out, x, not_1_out);
  and And2 (And2_out, not_2_out, y);
  or OR1 (o, And1_out, And2_out);

  // Notes on the sheet:
  //   Hier kan je een XOR-schakeling bouwen
  //   Je kan de tutorial volgen (in het Help-menu; "tutorial") of zelf de oplossing bedenken...
  //   XOR
endmodule

module FullAdder (
  input  X,
  input  Y,
  input  CarryIn,
  output Sum,
  output CarryOut
);

  wire A1_out, A_out, B1_out, B_out, C1_out, C_out, D1_out, D_out, not_1_out, not_2_out, not_3_out;

  not not_1 (not_1_out, X);
  not not_2 (not_2_out, Y);
  not not_3 (not_3_out, CarryIn);
  and A (A_out, not_1_out, not_2_out, CarryIn);
  and B (B_out, not_1_out, Y, not_3_out);
  and C (C_out, X, not_2_out, not_3_out);
  and D (D_out, X, Y, CarryIn);
  and A1 (A1_out, CarryIn, Y, not_1_out);
  and B1 (B1_out, CarryIn, not_2_out, X);
  and C1 (C1_out, not_3_out, Y, X);
  and D1 (D1_out, CarryIn, Y, X);
  or or1 (Sum, A_out, B_out, C_out, D_out);
  or or2 (CarryOut, A1_out, B1_out, C1_out, D1_out);

  // Notes on the sheet:
  //   3 invoerbits:  X,  Y en CarryIn
  //   Hier kan je een FULL-ADDERschakeling bouwen
  //   (1) teken de andere vier rails   (2) je hebt 8 AND-poorten nodig    (3)  je hebt twee OR-poorten nodig
  //   twee uitvoerbits:  Sum en CarryOut
endmodule

module Een_4bit_Ripple_Carry_Adder (
  input  X3,
  input  Y3,
  input  X2,
  input  Y2,
  input  X1,
  input  Y1,
  input  X0,
  input  Y0,
  output Sum4,
  output Sum3,
  output Sum2,
  output Sum1,
  output Sum0
);

  wire fulladder_2_carryout, fulladder_3_carryout, fulladder_4_carryout;

  FullAdder fulladder_1 (.X(X3), .Y(Y3), .CarryIn(fulladder_2_carryout), .Sum(Sum3), .CarryOut(Sum4));
  FullAdder fulladder_2 (.X(X2), .Y(Y2), .CarryIn(fulladder_3_carryout), .Sum(Sum2), .CarryOut(fulladder_2_carryout));
  FullAdder fulladder_3 (.X(X1), .Y(Y1), .CarryIn(fulladder_4_carryout), .Sum(Sum1), .CarryOut(fulladder_3_carryout));
  FullAdder fulladder_4 (.X(X0), .Y(Y0), .CarryIn(1'b0), .Sum(Sum0), .CarryOut(fulladder_4_carryout));

  // Notes on the sheet:
  //   Hier kan je een 4-bit-RIPPLE-CARRY-ADDERschakeling bouwen
  //   5 uitvoerbits
  //   8 invoerbits
endmodule

module Een_4bit_vermenigvuldiger (
  input  Y3,
  input  Y2,
  input  Y1,
  input  Y0,
  input  X3,
  input  X2,
  input  X1,
  input  X0,
  output Z7,
  output Z6,
  output Z5,
  output Z4,
  output Z3,
  output Z2,
  output Z1,
  output Z0
);

  wire een_4bit_ripple_carry_adder_2_sum1, een_4bit_ripple_carry_adder_2_sum2,
       een_4bit_ripple_carry_adder_2_sum3, een_4bit_ripple_carry_adder_2_sum4, een_4x1_vermenigvuldiger_1_z0,
       een_4x1_vermenigvuldiger_1_z1, een_4x1_vermenigvuldiger_1_z2, een_4x1_vermenigvuldiger_1_z3,
       een_4x1_vermenigvuldiger_2_z0, een_4x1_vermenigvuldiger_2_z1, een_4x1_vermenigvuldiger_2_z2,
       een_4x1_vermenigvuldiger_2_z3, een_4x1_vermenigvuldiger_3_z0, een_4x1_vermenigvuldiger_3_z1,
       een_4x1_vermenigvuldiger_3_z2, een_4x1_vermenigvuldiger_3_z3, een_4x1_vermenigvuldiger_4_z1,
       een_4x1_vermenigvuldiger_4_z2, een_4x1_vermenigvuldiger_4_z3;

  Een_4x1_vermenigvuldiger een_4x1_vermenigvuldiger_1 (
    .X(X3), .Y3(Y3), .Y2(Y2), .Y1(Y1), .Y0(Y0), .Z3(een_4x1_vermenigvuldiger_1_z3),
    .Z2(een_4x1_vermenigvuldiger_1_z2), .Z1(een_4x1_vermenigvuldiger_1_z1), .Z0(een_4x1_vermenigvuldiger_1_z0));
  Een_4x1_vermenigvuldiger een_4x1_vermenigvuldiger_2 (
    .X(X2), .Y3(Y3), .Y2(Y2), .Y1(Y1), .Y0(Y0), .Z3(een_4x1_vermenigvuldiger_2_z3),
    .Z2(een_4x1_vermenigvuldiger_2_z2), .Z1(een_4x1_vermenigvuldiger_2_z1), .Z0(een_4x1_vermenigvuldiger_2_z0));
  Een_4x1_vermenigvuldiger een_4x1_vermenigvuldiger_3 (
    .X(X1), .Y3(Y3), .Y2(Y2), .Y1(Y1), .Y0(Y0), .Z3(een_4x1_vermenigvuldiger_3_z3),
    .Z2(een_4x1_vermenigvuldiger_3_z2), .Z1(een_4x1_vermenigvuldiger_3_z1), .Z0(een_4x1_vermenigvuldiger_3_z0));
  Een_4x1_vermenigvuldiger een_4x1_vermenigvuldiger_4 (
    .X(X0), .Y3(Y3), .Y2(Y2), .Y1(Y1), .Y0(Y0), .Z3(een_4x1_vermenigvuldiger_4_z3),
    .Z2(een_4x1_vermenigvuldiger_4_z2), .Z1(een_4x1_vermenigvuldiger_4_z1), .Z0(Z0));
  Een_4bit_Ripple_Carry_Adder een_4bit_ripple_carry_adder_1 (
    .X3(een_4x1_vermenigvuldiger_4_z3), .Y3(een_4x1_vermenigvuldiger_3_z3),
    .X2(een_4x1_vermenigvuldiger_4_z2), .Y2(een_4x1_vermenigvuldiger_3_z2),
    .X1(een_4x1_vermenigvuldiger_4_z1), .Y1(een_4x1_vermenigvuldiger_3_z1), .X0(1'b0),
    .Y0(een_4x1_vermenigvuldiger_3_z0), .Sum4(Z1), .Sum3(Z1), .Sum2(Z1), .Sum1(Z1), .Sum0(Z1));
  Een_4bit_Ripple_Carry_Adder een_4bit_ripple_carry_adder_2 (
    .X3(Z1), .Y3(een_4x1_vermenigvuldiger_2_z3), .X2(Z1), .Y2(een_4x1_vermenigvuldiger_2_z2), .X1(Z1),
    .Y1(een_4x1_vermenigvuldiger_2_z1), .X0(Z1), .Y0(een_4x1_vermenigvuldiger_2_z0),
    .Sum4(een_4bit_ripple_carry_adder_2_sum4), .Sum3(een_4bit_ripple_carry_adder_2_sum3),
    .Sum2(een_4bit_ripple_carry_adder_2_sum2), .Sum1(een_4bit_ripple_carry_adder_2_sum1), .Sum0(Z2));
  Een_4bit_Ripple_Carry_Adder een_4bit_ripple_carry_adder_3 (
    .X3(een_4bit_ripple_carry_adder_2_sum4), .Y3(een_4x1_vermenigvuldiger_1_z3),
    .X2(een_4bit_ripple_carry_adder_2_sum3), .Y2(een_4x1_vermenigvuldiger_1_z2),
    .X1(een_4bit_ripple_carry_adder_2_sum2), .Y1(een_4x1_vermenigvuldiger_1_z1),
    .X0(een_4bit_ripple_carry_adder_2_sum1), .Y0(een_4x1_vermenigvuldiger_1_z0), .Sum4(Z7), .Sum3(Z6),
    .Sum2(Z5), .Sum1(Z4), .Sum0(Z3));

  // Notes on the sheet:
  //   factor (4 bits)
  //   tweede factor (4 bits)
  //   4-bit-VERMENIGVULDIGINGSschakeling
  //   meest significante (hoogste) uitvoerbit
endmodule

module Een_3bij2_deler (
  input  Y2,
  input  Y1,
  input  Y0,
  input  X1,
  input  X0,
  output Z2,
  output Z1,
  output Z0,
  output Error
);

  wire and_1_out, and_2_out, and_3_out, and_5_out, and_6_out, and_7_out, and_8_out, and_9_out, and_10_out,
       not_1_out, not_2_out, not_3_out, not_4_out, not_5_out, not_6_out, not_7_out, not_8_out, not_9_out,
       not_10_out, not_11_out, or_1_out;

  not not_1 (not_1_out, Y0);
  not not_2 (not_2_out, Y1);
  not not_3 (not_3_out, Y2);
  not not_4 (not_4_out, Y1);
  and and_1 (and_1_out, Y2, not_1_out, not_2_out);
  and and_2 (and_2_out, not_3_out, Y1, Y0);
  and and_3 (and_3_out, Y2, not_4_out, Y0);
  or or_1 (or_1_out, and_1_out, and_2_out, and_3_out);
  not not_5 (not_5_out, X1);
  not not_6 (not_6_out, X1);
  not not_7 (not_7_out, X0);
  not not_8 (not_8_out, X1);
  not not_9 (not_9_out, X0);
  and and_4 (Z2, X0, not_5_out, Y2);
  and and_5 (and_5_out, X1, Y1, Y2);
  and and_6 (and_6_out, X0, not_6_out, Y1);
  and and_7 (and_7_out, Y2, not_7_out);
  and and_8 (and_8_out, X0, not_8_out, Y0);
  and and_9 (and_9_out, Y1, not_9_out, X1);
  and and_10 (and_10_out, or_1_out, X1, X0);
  or or_2 (Z1, and_5_out, and_6_out, and_7_out);
  or or_3 (Z0, and_8_out, and_9_out, and_10_out);
  not not_10 (not_10_out, X0);
  not not_11 (not_11_out, X1);
  and and_11 (Error, not_10_out, not_11_out);

  // Notes on the sheet:
  //   Teller (3 bits: Y2 Y1 Y0)
  //   Noemer (2 bits: X1 X0)
  //   Quotiënt (4 bits: Z2 Z1 Z0 en Error)
  //   3-bij-2-bit-DELINGSschakeling
endmodule

module Een_2bit_decoder (
);


  // Notes on the sheet:
  //   2-bit-DECODERschakeling (bonusopgave)
endmodule

module Een_12nGb_geheugen (
);


  // Notes on the sheet:
  //   12-nanogigabit-GEHEUGENschakelin (bonusopgave)
endmodule

module Een_4x1_vermenigvuldiger (
  input  Y3,
  input  Y2,
  input  Y1,
  input  Y0,
  input  X,
  output Z3,
  output Z2,
  output Z1,
  output Z0
);

  and and_1 (Z3, X, Y3);
  and and_2 (Z2, X, Y2);
  and and_3 (Z1, X, Y1);
  and and_4 (Z0, X, Y0);
endmodule
